# Fritzing sketch streamNode (saved by Fritzing 0.9.0b)

parts:
  pH_Circuit1 = pH Circuit
  Part_1 = Weather Shield [part_number=DEV-12081]
  Part2 = Arduino Mega 2560 (Rev3)
  Pre-Assembled_Female_BNC1 = Pre-Assembled Female BNC
  J1 = RJ11 Jack [package=rj11-6]
  J2 = RJ11 Jack [package=rj11-6]
  J3 = Infrared Proximity Sensor
  J4 = Infrared Proximity Sensor
  R1 = PHOTOCELL [package=photocell-kit]
  LED2 = LEDs [package=led-1206]
  R2 = Resistor [tolerance=±5% resistance=100 package=THT]
  DS1 = DS18B20 1-Wire Temperature Sensor [part_number=DS18B20]
  PART1 = CC3000 WiFi Breakout Board [part_number=WRL-12072]

nets:
  GND: pH_Circuit1.GND, Part_1.D5, Part_1.GND, Part2.GND, Part2.D5_PWM, Pre-Assembled_Female_BNC1.GND, J3.GND, J4.GND, R1.P$1, LED2.C, DS1.GND, PART1.GND
  N1: pH_Circuit1.TX, Part2.D17_PWM/RX2
  N2: pH_Circuit1.RX, Part2.D16_PWM/TX2
  VCC: pH_Circuit1.Vcc, Part_1.5V, Part2.5V, J3.Vcc, J4.Vcc, R2.Pin_0, DS1.VDD, PART1.VCC
  N3: pH_Circuit1.PRB, Pre-Assembled_Female_BNC1.PRB
  N4: Part_1.RX, Part2.D0_RX0
  N5: Part_1.TX, Part2.D1_TX0
  N6: Part_1.D2, Part2.D2_PWM
  N7: Part_1.D3, Part2.D3_PWM
  VIN: Part_1.D4, Part_1.VIN, Part2.VIN, Part2.D4_PWM
  N8: Part_1.D6, Part_1.D11, Part_1.RAIN_PIN_5, Part2.D11_PWM, Part2.D6_PWM, J2.5
  N9: Part_1.D7, Part_1.A4, Part2.A4, Part2.D7_PWM
  N10: Part_1.D8, Part_1.RAIN_PIN_3, Part2.D8_PWM, J2.3
  N11: Part_1.D9, Part_1.AREF, Part_1.A1, Part_1.RAIN_PIN_6, Part_1.WIND_PIN_1, Part2.A1, Part2.AREF, Part2.D9_PWM, J1.1, J2.6
  N12: Part_1.D10, Part2.D10_PWM
  N13: Part_1.D12, Part2.D12_PWM
  N14: Part_1.D13, Part2.D13_PWM
  N15: Part_1.SDA, Part2.SDA
  N16: Part_1.SCL, Part2.D21/SCL, Part2.SCL, PART1.INT
  N17: Part_1.A5, Part2.A5
  N18: Part_1.A3, Part2.A3
  N19: Part_1.A2, Part2.A2
  N20: Part_1.A0, Part2.A0
  3.3V: Part_1.3.3V, Part2.3V3, PART1.3.3V
  N21: Part_1.RST, Part2.RESET
  N22: Part_1.IOREF, Part2.IOREF
  N23: Part_1.RAIN_PIN_1, J2.1
  N24: Part_1.RAIN_PIN_2, J2.2
  N25: Part_1.RAIN_PIN_4, J2.4
  N26: Part_1.WIND_PIN_2, J1.2
  N27: Part_1.WIND_PIN_3, J1.3
  N28: Part_1.WIND_PIN_4, J1.4
  N29: Part_1.WIND_PIN_5, J1.5
  N30: Part_1.WIND_PIN_6, J1.6
  N31: Part2.A8, R1.P$2, R2.Pin_1
  N32: Part2.A6, J4.Vout
  N33: Part2.A7, J3.Vout
  N34: Part2.D18/TX1, PART1.EN
  N35: Part2.D15/RX3, DS1.DQ
  N36: Part2.D14/TX3, LED2.A
  N37: Part2.D50, PART1.MISO
  N38: Part2.D51, PART1.MOSI
  N39: Part2.D52, PART1.SCK
  N40: Part2.D53, PART1.CS

custom parts:
  Weather Shield: Weather Shield includes: - ALS-PT19 Light Sensor - HTU21D Humidity Sensor - MPL3115A2 - TEMT6000 Check out the product page on www.sparkfun.com for documentation!
  CC3000 WiFi Breakout Board: Breakout board for TI CC3000 WiFi module.
